# Fritzing sketch rupibox_sketch (saved by Fritzing 0.9.2b)
breadboards: 1

parts:
  Raspberry_Pi_B_rev1 = Raspberry Pi B rev1
  U1 = 2-Channel 5v Relay Shield [package=relay-2ch5v10a]
  U2 = 2-Channel 5v Relay Shield [package=relay-2ch5v10a]

nets:
  VCC: Raspberry_Pi_B_rev1.5V, U1.VCC, U2.VCC
  N1: Raspberry_Pi_B_rev1.GPIO_23, U1.IN2
  N2: Raspberry_Pi_B_rev1.GPIO_17, U1.IN1
  N3: Raspberry_Pi_B_rev1.GPIO_21, U2.IN1
  N4: Raspberry_Pi_B_rev1.GPIO_22, U2.IN2
  GND: Raspberry_Pi_B_rev1.GND, U1.GND, U2.GND

custom parts:
  2-Channel 5v Relay Shield: 2 Channel 5v Relay Shield w. 2x SPD-06VDC-SD-C
